# Fritzing sketch walrusgand-Fritz (saved by Fritzing 0.9.3b)
breadboards: 1

parts:
  LM2596 = LM2596 step down module
  Arduino = Arduino Nano (Rev3.0) (ICSP)
  R2 = Resistor [tolerance=±5% resistance=220 package="0402 [SMD]"]
  R1 = Resistor [tolerance=±5% resistance=100 package="0805 [SMD]"]
  12V_DC = Power plug
  Reader_1 = female pin header, 4 pins [form="♀ (female)"]
  Reader_3 = female pin header, 4 pins [form="♀ (female)"]
  Reader_2 = female pin header, 4 pins [form="♀ (female)"]
  Bluetooth_Module = Bluetooth HC-05 Macho

nets (from the breadboard view):
  N1: LM2596.IN+, 12V_DC.VCC, Reader_1.pin1, Reader_3.pin1, Reader_2.pin1
  GND: LM2596.IN-, LM2596.OUT-, Arduino.GND, R2.Pin_0, 12V_DC.GND, Reader_1.pin2, Reader_3.pin2, Reader_2.pin2, Bluetooth_Module.GND
  VIN: LM2596.OUT+, Arduino.VIN, Bluetooth_Module.VCC
  N2: Arduino.D1/TX, R1.Pin_0
  N3: Arduino.D0/RX, Bluetooth_Module.TXD
  N4: Arduino.D2, Reader_1.pin3
  N5: Arduino.D3, Reader_1.pin4
  N6: Arduino.D4, Reader_2.pin3
  N7: Arduino.D5, Reader_2.pin4
  N8: Arduino.D6, Reader_3.pin3
  N9: Arduino.D7, Reader_3.pin4
  N10: R2.Pin_1, R1.Pin_1, Bluetooth_Module.RXD

custom parts:
  LM2596 step down module: LM2596 DC-DC step down power supply module 3 A.
